# Fritzing sketch motion circuit (saved by Fritzing 0.9.3b)

parts:
  Part1 = Arduino Uno (Rev3)  # not connected
  Part2 = Rotoshield - Motor driver shield for Arduino
  L1 = Solenoid
  L2 = Solenoid
  L3 = Solenoid
  Part3 = Arduino Uno (Rev3)
  J1 = Basic Servo

nets:
  N1: Part2.GND, L1.pin2, L2.pin2, L3.pin2
  N2: Part2.M1-1, L2.pin1
  N3: Part2.M2-1, L3.pin1
  N4: Part2.M3-1, L1.pin1
  5V: Part3.5V, J1.vcc
  GND: Part3.GND, J1.gnd
